// Logisim project control-logic.circ as structural Verilog: 1 circuit, main circuit control_logic
module control_logic (
  input  [31:0] Instruction,
  input  BrEq,
  input  BrLt,
  output PCSel,
  output RegWEn,
  output [2:0] ImmSel,
  output BrUn,
  output ASel,
  output BSel,
  output [3:0] ALUSel,
  output MemWEn,
  output [1:0] WBSel
);

  wire and_13_out, and_14_out, and_15_out, and_16_out, comparator_1_eq, comparator_2_eq, comparator_3_eq,
       comparator_13_eq, comparator_14_eq, comparator_15_eq, comparator_16_eq, comparator_17_eq,
       comparator_18_eq, comparator_19_eq, comparator_20_eq, comparator_21_eq, comparator_22_eq,
       comparator_23_eq, comparator_24_eq, comparator_25_eq, comparator_26_eq, comparator_27_eq,
       comparator_28_eq, comparator_29_eq, comparator_30_eq, comparator_31_eq, comparator_32_eq,
       comparator_33_eq, comparator_34_eq, comparator_35_eq, comparator_36_eq, comparator_37_eq,
       comparator_38_eq, comparator_39_eq, comparator_40_eq, comparator_41_eq, is_add, is_addi, is_and,
       is_andi, is_auipc, is_B, is_beq, is_bge, is_bgeu, is_blt, is_bltu, is_bne, is_I, is_I_sharp, is_jal,
       is_jalr, is_lb, is_lh, is_lui, is_lw, is_mul, is_mulh, is_mulhu, is_or, is_ori, is_R, is_S, is_sb,
       is_sh, is_sll, is_slli, is_slt, is_slti, is_sra, is_srai, is_srl, is_srli, is_sub, is_sw, is_xor,
       is_xori, not_1_out, not_2_out, not_3_out, not_4_out, not_5_out, not_6_out, not_7_out, not_8_out,
       not_9_out, not_10_out, or_1_out, or_2_out;
  wire [5:0] SelIndex;
  wire [15:14] rom_1_data;

  ROM #(.addrWidth(6), .dataWidth(16)) rom_1 (
    .addr(SelIndex), .data({rom_1_data, WBSel, MemWEn, ALUSel, BSel, ASel, BrUn, ImmSel, RegWEn}));
  // Priority_Encoder #(.select_enc(6)) priority_encoder_1: pin names not known; wires that end beside it: is_xor, is_srl, is_sra, is_or, is_and, is_lb, is_lh, is_lw, is_addi, is_slli, is_slti, is_xori, is_srli, is_srai, is_ori, is_andi, is_sb, is_sh, is_sw, is_beq, is_bne, is_blt, is_bge, is_bltu, SelIndex, is_bgeu, is_auipc, is_lui, is_jal, is_jalr
  Comparator #(.width(3)) comparator_1 (.a(Instruction[14:12]), .b(3'b000), .eq(comparator_1_eq));  // open: gt, lt
  Comparator #(.width(3)) comparator_2 (.a(Instruction[14:12]), .b(3'b001), .eq(comparator_2_eq));  // open: gt, lt
  Comparator #(.width(3)) comparator_3 (.a(Instruction[14:12]), .b(3'b011), .eq(comparator_3_eq));  // open: gt, lt
  Comparator #(.mode("unsigned"), .width(5)) comparator_4 (
    .a(Instruction[6:2]), .b(5'b01100), .eq(is_R));  // open: gt, lt
  Comparator #(.mode("unsigned"), .width(5)) comparator_5 (
    .a(Instruction[6:2]), .b({5{1'b0}}), .eq(is_I_sharp));  // open: gt, lt
  Comparator #(.mode("unsigned"), .width(5)) comparator_6 (
    .a(Instruction[6:2]), .b(5'b00100), .eq(is_I));  // open: gt, lt
  Comparator #(.mode("unsigned"), .width(5)) comparator_7 (
    .a(Instruction[6:2]), .b(5'b11001), .eq(is_jalr));  // open: gt, lt
  Comparator #(.mode("unsigned"), .width(5)) comparator_8 (
    .a(Instruction[6:2]), .b(5'b01000), .eq(is_S));  // open: gt, lt
  Comparator #(.mode("unsigned"), .width(5)) comparator_9 (
    .a(Instruction[6:2]), .b(5'b11000), .eq(is_B));  // open: gt, lt
  and and_1 (is_mul, Instruction[25], is_R, comparator_1_eq);
  and and_2 (is_mulh, Instruction[25], is_R, comparator_2_eq);
  and and_3 (is_mulhu, Instruction[25], is_R, comparator_3_eq);
  Comparator #(.mode("unsigned"), .width(5)) comparator_10 (
    .a(Instruction[6:2]), .b(5'b11011), .eq(is_jal));  // open: gt, lt
  Comparator #(.mode("unsigned"), .width(5)) comparator_11 (
    .a(Instruction[6:2]), .b(5'b01101), .eq(is_lui));  // open: gt, lt
  Comparator #(.mode("unsigned"), .width(5)) comparator_12 (
    .a(Instruction[6:2]), .b(5'b00101), .eq(is_auipc));  // open: gt, lt
  not not_1 (not_1_out, Instruction[30]);
  Comparator #(.width(3)) comparator_13 (.a(Instruction[14:12]), .b(3'b000), .eq(comparator_13_eq));  // open: gt, lt
  Comparator #(.width(3)) comparator_14 (.a(Instruction[14:12]), .b(3'b000), .eq(comparator_14_eq));  // open: gt, lt
  not not_2 (not_2_out, Instruction[30]);
  Comparator #(.width(3)) comparator_15 (.a(Instruction[14:12]), .b(3'b001), .eq(comparator_15_eq));  // open: gt, lt
  not not_3 (not_3_out, Instruction[30]);
  Comparator #(.width(3)) comparator_16 (.a(Instruction[14:12]), .b(3'b010), .eq(comparator_16_eq));  // open: gt, lt
  not not_4 (not_4_out, Instruction[30]);
  Comparator #(.width(3)) comparator_17 (.a(Instruction[14:12]), .b(3'b100), .eq(comparator_17_eq));  // open: gt, lt
  not not_5 (not_5_out, Instruction[30]);
  Comparator #(.width(3)) comparator_18 (.a(Instruction[14:12]), .b(3'b101), .eq(comparator_18_eq));  // open: gt, lt
  Comparator #(.width(3)) comparator_19 (.a(Instruction[14:12]), .b(3'b101), .eq(comparator_19_eq));  // open: gt, lt
  not not_6 (not_6_out, Instruction[30]);
  Comparator #(.width(3)) comparator_20 (.a(Instruction[14:12]), .b(3'b110), .eq(comparator_20_eq));  // open: gt, lt
  not not_7 (not_7_out, Instruction[30]);
  Comparator #(.width(3)) comparator_21 (.a(Instruction[14:12]), .b(3'b111), .eq(comparator_21_eq));  // open: gt, lt
  and and_4 (is_add, is_R, not_1_out, comparator_13_eq);
  and and_5 (is_sub, is_R, Instruction[30], comparator_14_eq);
  and and_6 (is_sll, is_R, not_2_out, comparator_15_eq);
  and and_7 (is_slt, is_R, not_3_out, comparator_16_eq);
  and and_8 (is_xor, is_R, not_4_out, comparator_17_eq);
  and and_9 (is_srl, is_R, not_5_out, comparator_18_eq);
  and and_10 (is_sra, is_R, Instruction[30], comparator_19_eq);
  and and_11 (is_or, is_R, not_6_out, comparator_20_eq);
  and and_12 (is_and, is_R, not_7_out, comparator_21_eq);
  and and_13 (and_13_out, BrLt, or_1_out);
  or or_1 (or_1_out, is_blt, is_bltu);
  not not_8 (not_8_out, BrLt);
  and and_14 (and_14_out, not_8_out, or_2_out);
  or or_2 (or_2_out, is_bge, is_bgeu);
  and and_15 (and_15_out, BrEq, is_beq);
  not not_9 (not_9_out, BrEq);
  and and_16 (and_16_out, not_9_out, is_bne);
  Comparator #(.width(3)) comparator_22 (.a(Instruction[14:12]), .b(3'b000), .eq(comparator_22_eq));  // open: gt, lt
  Comparator #(.width(3)) comparator_23 (.a(Instruction[14:12]), .b(3'b001), .eq(comparator_23_eq));  // open: gt, lt
  Comparator #(.width(3)) comparator_24 (.a(Instruction[14:12]), .b(3'b010), .eq(comparator_24_eq));  // open: gt, lt
  Comparator #(.width(3)) comparator_25 (.a(Instruction[14:12]), .b(3'b100), .eq(comparator_25_eq));  // open: gt, lt
  not not_10 (not_10_out, Instruction[30]);
  Comparator #(.width(3)) comparator_26 (.a(Instruction[14:12]), .b(3'b101), .eq(comparator_26_eq));  // open: gt, lt
  Comparator #(.width(3)) comparator_27 (.a(Instruction[14:12]), .b(3'b101), .eq(comparator_27_eq));  // open: gt, lt
  Comparator #(.width(3)) comparator_28 (.a(Instruction[14:12]), .b(3'b110), .eq(comparator_28_eq));  // open: gt, lt
  Comparator #(.width(3)) comparator_29 (.a(Instruction[14:12]), .b(3'b111), .eq(comparator_29_eq));  // open: gt, lt
  and and_17 (is_addi, is_I, comparator_22_eq);
  and and_18 (is_slli, is_I, comparator_23_eq);
  and and_19 (is_slti, is_I, comparator_24_eq);
  and and_20 (is_xori, is_I, comparator_25_eq);
  and and_21 (is_srli, is_I, not_10_out, comparator_26_eq);
  and and_22 (is_srai, is_I, Instruction[30], comparator_27_eq);
  and and_23 (is_ori, is_I, comparator_28_eq);
  and and_24 (is_andi, is_I, comparator_29_eq);
  or or_3 (PCSel, and_13_out, and_14_out, and_15_out, and_16_out, is_jalr, is_jal);
  Comparator #(.width(3)) comparator_30 (.a(Instruction[14:12]), .b(3'b000), .eq(comparator_30_eq));  // open: gt, lt
  Comparator #(.width(3)) comparator_31 (.a(Instruction[14:12]), .b(3'b001), .eq(comparator_31_eq));  // open: gt, lt
  Comparator #(.width(3)) comparator_32 (.a(Instruction[14:12]), .b(3'b010), .eq(comparator_32_eq));  // open: gt, lt
  Comparator #(.width(3)) comparator_33 (.a(Instruction[14:12]), .b(3'b000), .eq(comparator_33_eq));  // open: gt, lt
  Comparator #(.width(3)) comparator_34 (.a(Instruction[14:12]), .b(3'b001), .eq(comparator_34_eq));  // open: gt, lt
  Comparator #(.width(3)) comparator_35 (.a(Instruction[14:12]), .b(3'b010), .eq(comparator_35_eq));  // open: gt, lt
  and and_25 (is_lb, is_I_sharp, comparator_30_eq);
  and and_26 (is_lh, is_I_sharp, comparator_31_eq);
  and and_27 (is_lw, is_I_sharp, comparator_32_eq);
  and and_28 (is_sb, is_S, comparator_33_eq);
  and and_29 (is_sh, is_S, comparator_34_eq);
  and and_30 (is_sw, is_S, comparator_35_eq);
  Comparator #(.width(3)) comparator_36 (.a(Instruction[14:12]), .b(3'b000), .eq(comparator_36_eq));  // open: gt, lt
  Comparator #(.width(3)) comparator_37 (.a(Instruction[14:12]), .b(3'b001), .eq(comparator_37_eq));  // open: gt, lt
  Comparator #(.width(3)) comparator_38 (.a(Instruction[14:12]), .b(3'b100), .eq(comparator_38_eq));  // open: gt, lt
  Comparator #(.width(3)) comparator_39 (.a(Instruction[14:12]), .b(3'b101), .eq(comparator_39_eq));  // open: gt, lt
  Comparator #(.width(3)) comparator_40 (.a(Instruction[14:12]), .b(3'b110), .eq(comparator_40_eq));  // open: gt, lt
  Comparator #(.width(3)) comparator_41 (.a(Instruction[14:12]), .b(3'b111), .eq(comparator_41_eq));  // open: gt, lt
  and and_31 (is_beq, is_B, comparator_36_eq);
  and and_32 (is_bne, is_B, comparator_37_eq);
  and and_33 (is_blt, is_B, comparator_38_eq);
  and and_34 (is_bge, is_B, comparator_39_eq);
  and and_35 (is_bltu, is_B, comparator_40_eq);
  and and_36 (is_bgeu, is_B, comparator_41_eq);

  // Other names for the same wires on the sheet: opcode[6:0] = Instruction[6:0]; rd[4:0] = Instruction[11:7];
  //   funt3[2:0] = Instruction[14:12]; rs1[4:0] = Instruction[19:15]; rs2[4:0] = Instruction[24:20];
  //   funt7[6:0] = Instruction[31:25]

  // Notes on the sheet:
  //   INPUTS to your circuit
  //   contents of rom_1 (hex, n*v repeats v):
  //   1001 1401 1601 1081 1481 1581 1101 1201 1281 1681 1301 1381 41 41 41 1041 10c1 1141 1241 12c1 16c1
  //   1341 13c1 842 842 842 4*64 74 74 1067 17c7 2069 2041
  //   ROM FOR CONTROL LOGIC
  //   DON'T CHANGE THE LOCATIONS OF THE INPUTS AND OUTPUTS!
  //   This is only if you choose to do the ROM option
  //   OUTPUT from your circuit
endmodule
