// Logisim project partial-store.circ as structural Verilog: 1 circuit, main circuit partial_store
module partial_store (
  input  [31:0] Instruction,
  input  [31:0] MemAddress,
  input  [31:0] DataFromReg,
  input  MemWEn,
  output [3:0] MemWriteMask,
  output [31:0] DataToMem
);

  wire is_sb, is_sh, is_sw;
  wire [3:0] MemWriteMasksb, MemWriteMasksh;
  wire [31:0] DataToMemsb, DataToMemsh;

  Decoder #(.select(3)) decoder_1 (
    .out0(is_sb), .out1(is_sh), .out2(is_sw), .sel(Instruction[14:12]), .en(MemWEn));  // open: out3, out4, out5, out6, out7
  Multiplexer #(.enable("true"), .select(3), .width(4)) multiplexer_1 (
    .in0(MemWriteMasksb), .in1(MemWriteMasksh), .in2(4'b1111), .out(MemWriteMask), .sel(Instruction[14:12]),
    .en(MemWEn));  // open: in3, in4, in5, in6, in7
  Multiplexer #(.enable("true"), .select(3), .width(32)) multiplexer_2 (
    .in0(DataToMemsb), .in1(DataToMemsh), .in2(DataFromReg), .out(DataToMem), .sel(Instruction[14:12]),
    .en(MemWEn));  // open: in3, in4, in5, in6, in7
  Multiplexer #(.enable("true"), .select(2), .width(4)) multiplexer_3 (
    .in0(4'b0001), .in1(4'b0010), .in2(4'b0100), .in3(4'b1000), .out(MemWriteMasksb), .sel(MemAddress[1:0]),
    .en(is_sb));
  Multiplexer #(.enable("true"), .select(2), .width(4)) multiplexer_4 (
    .in0(4'b0011), .in2(4'b1100), .out(MemWriteMasksh), .sel(MemAddress[1:0]), .en(is_sh));  // open: in1, in3
  Multiplexer #(.enable("true"), .select(2), .width(32)) multiplexer_5 (
    .in0({{24{1'b0}}, DataFromReg[7:0]}), .in1({{16{1'b0}}, DataFromReg[7:0], {8{1'b0}}}),
    .in2({{8{1'b0}}, DataFromReg[7:0], {16{1'b0}}}), .in3({DataFromReg[7:0], {24{1'b0}}}), .out(DataToMemsb),
    .sel(MemAddress[1:0]), .en(is_sb));
  Multiplexer #(.enable("true"), .select(2), .width(32)) multiplexer_6 (
    .in0({{16{1'b0}}, DataFromReg[15:0]}), .in2({DataFromReg[15:0], {16{1'b0}}}), .out(DataToMemsh),
    .sel(MemAddress[1:0]), .en(is_sh));  // open: in1, in3

  // Other names for the same wires on the sheet: DataToMemsw[31:0] = DataFromReg; opcode[6:0] = Instruction[6:0];
  //   rd[4:0] = Instruction[11:7]; funt3[2:0] = Instruction[14:12]; rs1[4:0] = Instruction[19:15];
  //   rs2[4:0] = Instruction[24:20]; funt7[6:0] = Instruction[31:25]

  // Notes on the sheet:
  //   INPUTS to your circuit
  //   DON'T CHANGE THE LOCATIONS OF THE INPUTS AND OUTPUTS!
  //   OUTPUT from your circuit
endmodule
